# Fritzing sketch schematic (saved by Fritzing 0.9.2b)
breadboards: 1

parts:
  LED1 = smd LED [color="Red (633nm)" package="0603 [SMD]"]
  R1 = Resistor [tolerance=±5% resistance=220 package="0603 [SMD]"]
  Raspberry_Pi2 = Raspberry Pi B rev2
  Door_#1 = Magnetic Door Switch [package=reed_switch_plastic]
  Door_#2 = Magnetic Door Switch [package=reed_switch_plastic]

nets:
  N1: LED1.cathode, R1.Pin_1
  N2: LED1.anode, Raspberry_Pi2.GPIO_17
  N3: Raspberry_Pi2.GND, Door_#1.2, Door_#2.2
  N4: Raspberry_Pi2.GPIO_4, Door_#1.1
  N5: Raspberry_Pi2.GPIO_24, Door_#2.1
